// Logisim project CODE.circ as structural Verilog
module XOR (
  input  A_In,
  input  B_In,
  output Out
);

  wire nand_1_out, or_1_out;

  or or_1 (or_1_out, A_In, B_In);
  nand nand_1 (nand_1_out, A_In, B_In);
  and and_1 (Out, or_1_out, nand_1_out);
endmodule

module Half_Adder (
  input  A_In,
  input  B_In,
  output Sum_Out,
  output Carry_Out
);

  XOR xor_1 (.A_In(A_In), .B_In(B_In), .Out(Sum_Out));
  and and_1 (Carry_Out, A_In, B_In);
endmodule

module Full_Adder (
  input  Carry_In,
  input  A_In,
  input  B_In,
  output Sum_Out,
  output Carry_Out
);

  wire half_adder_1_carry_out, half_adder_1_sum_out, half_adder_2_carry_out;

  Half_Adder half_adder_1 (
    .A_In(A_In), .B_In(B_In), .Sum_Out(half_adder_1_sum_out), .Carry_Out(half_adder_1_carry_out));
  Half_Adder half_adder_2 (
    .A_In(Carry_In), .B_In(half_adder_1_sum_out), .Sum_Out(Sum_Out), .Carry_Out(half_adder_2_carry_out));
  or or_1 (Carry_Out, half_adder_2_carry_out, half_adder_1_carry_out);
endmodule

module _8_Bit_Adder (
  input  Carry_In,
  input  [7:0] BIn8_0to7,
  input  [7:0] AIn_0to7,
  output [7:0] SumOut8_0to7,
  output Carry_Out
);

  wire full_adder_1_carry_out, full_adder_2_carry_out, full_adder_3_carry_out, full_adder_4_carry_out,
       full_adder_5_carry_out, full_adder_6_carry_out, full_adder_7_carry_out;

  Full_Adder full_adder_1 (
    .A_In(AIn_0to7[0]), .B_In(BIn8_0to7[0]), .Carry_In(Carry_In), .Carry_Out(full_adder_1_carry_out),
    .Sum_Out(SumOut8_0to7[0]));
  Full_Adder full_adder_2 (
    .A_In(AIn_0to7[1]), .B_In(BIn8_0to7[1]), .Carry_In(full_adder_1_carry_out),
    .Carry_Out(full_adder_2_carry_out), .Sum_Out(SumOut8_0to7[1]));
  Full_Adder full_adder_3 (
    .A_In(AIn_0to7[2]), .B_In(BIn8_0to7[2]), .Carry_In(full_adder_2_carry_out),
    .Carry_Out(full_adder_3_carry_out), .Sum_Out(SumOut8_0to7[2]));
  Full_Adder full_adder_4 (
    .A_In(AIn_0to7[3]), .B_In(BIn8_0to7[3]), .Carry_In(full_adder_3_carry_out),
    .Carry_Out(full_adder_4_carry_out), .Sum_Out(SumOut8_0to7[3]));
  Full_Adder full_adder_5 (
    .A_In(AIn_0to7[4]), .B_In(BIn8_0to7[4]), .Carry_In(full_adder_4_carry_out),
    .Carry_Out(full_adder_5_carry_out), .Sum_Out(SumOut8_0to7[4]));
  Full_Adder full_adder_6 (
    .A_In(AIn_0to7[5]), .B_In(BIn8_0to7[5]), .Carry_In(full_adder_5_carry_out),
    .Carry_Out(full_adder_6_carry_out), .Sum_Out(SumOut8_0to7[5]));
  Full_Adder full_adder_7 (
    .A_In(AIn_0to7[6]), .B_In(BIn8_0to7[6]), .Carry_In(full_adder_6_carry_out),
    .Carry_Out(full_adder_7_carry_out), .Sum_Out(SumOut8_0to7[6]));
  Full_Adder full_adder_8 (
    .A_In(AIn_0to7[7]), .B_In(BIn8_0to7[7]), .Carry_In(full_adder_7_carry_out), .Carry_Out(Carry_Out),
    .Sum_Out(SumOut8_0to7[7]));
endmodule

module One_s_Compliment (
  input  Invert,
  input  [7:0] Input8_0to7,
  output [7:0] Output8_0to7
);

  XOR xor_1 (.A_In(Input8_0to7[0]), .B_In(Invert), .Out(Output8_0to7[0]));
  XOR xor_2 (.A_In(Input8_0to7[1]), .B_In(Invert), .Out(Output8_0to7[1]));
  XOR xor_3 (.A_In(Input8_0to7[2]), .B_In(Invert), .Out(Output8_0to7[2]));
  XOR xor_4 (.A_In(Input8_0to7[3]), .B_In(Invert), .Out(Output8_0to7[3]));
  XOR xor_5 (.A_In(Input8_0to7[4]), .B_In(Invert), .Out(Output8_0to7[4]));
  XOR xor_6 (.A_In(Input8_0to7[5]), .B_In(Invert), .Out(Output8_0to7[5]));
  XOR xor_7 (.A_In(Input8_0to7[6]), .B_In(Invert), .Out(Output8_0to7[6]));
  XOR xor_8 (.A_In(Input8_0to7[7]), .B_In(Invert), .Out(Output8_0to7[7]));
endmodule

module _8_Bit_Adder_Subtractor (
  input  Sub,
  input  [7:0] Subtrahand8_0to7,
  input  [7:0] Minuend8_0to7,
  output [7:0] SumOut8_0to7,
  output Overflow_Underflow
);

  wire n8_bit_adder_1_carry_out;
  wire [7:0] one_s_compliment_1_output8_0to7;

  One_s_Compliment one_s_compliment_1 (
    .Input8_0to7(Subtrahand8_0to7), .Invert(Sub), .Output8_0to7(one_s_compliment_1_output8_0to7));
  _8_Bit_Adder u_8_bit_adder_1 (
    .BIn8_0to7(one_s_compliment_1_output8_0to7), .AIn_0to7(Minuend8_0to7), .Carry_In(Sub),
    .Carry_Out(n8_bit_adder_1_carry_out), .SumOut8_0to7(SumOut8_0to7));
  XOR xor_1 (.A_In(Sub), .B_In(n8_bit_adder_1_carry_out), .Out(Overflow_Underflow));
endmodule

module R_S_Flip_Flop (
  input  R,
  input  S,
  output Q,
  output Q_Bar
);

  nor nor_1 (Q, R, Q_Bar);
  nor nor_2 (Q_Bar, Q, S);
endmodule

module Level_Triggered_D_Type_Flip_Flop (
  input  Clock,
  input  Data,
  output Q,
  output Q_Bar,
  output Clock_Out
);

  wire and_1_out, and_2_out, not_1_out;

  not not_1 (not_1_out, Data);
  and and_1 (and_1_out, not_1_out, Clock);
  and and_2 (and_2_out, Clock, Data);
  R_S_Flip_Flop r_s_ff_1 (.R(and_1_out), .S(and_2_out), .Q(Q), .Q_Bar(Q_Bar));

  assign Clock_Out = Clock;
endmodule

module _8_Bit_Latch (
  input  Clock,
  input  [7:0] Data,
  output [7:0] Q
);

  wire level_triggered_d_type_ff_1_clock_out, level_triggered_d_type_ff_2_clock_out,
       level_triggered_d_type_ff_3_clock_out, level_triggered_d_type_ff_4_clock_out,
       level_triggered_d_type_ff_5_clock_out, level_triggered_d_type_ff_6_clock_out,
       level_triggered_d_type_ff_7_clock_out;

  Level_Triggered_D_Type_Flip_Flop level_triggered_d_type_ff_1 (
    .Data(Data[0]), .Clock(Clock), .Clock_Out(level_triggered_d_type_ff_1_clock_out), .Q(Q[0]));  // open: Q_Bar
  Level_Triggered_D_Type_Flip_Flop level_triggered_d_type_ff_2 (
    .Data(Data[1]), .Clock(level_triggered_d_type_ff_1_clock_out),
    .Clock_Out(level_triggered_d_type_ff_2_clock_out), .Q(Q[1]));  // open: Q_Bar
  Level_Triggered_D_Type_Flip_Flop level_triggered_d_type_ff_3 (
    .Data(Data[2]), .Clock(level_triggered_d_type_ff_2_clock_out),
    .Clock_Out(level_triggered_d_type_ff_3_clock_out), .Q(Q[2]));  // open: Q_Bar
  Level_Triggered_D_Type_Flip_Flop level_triggered_d_type_ff_4 (
    .Data(Data[3]), .Clock(level_triggered_d_type_ff_3_clock_out),
    .Clock_Out(level_triggered_d_type_ff_4_clock_out), .Q(Q[3]));  // open: Q_Bar
  Level_Triggered_D_Type_Flip_Flop level_triggered_d_type_ff_5 (
    .Data(Data[4]), .Clock(level_triggered_d_type_ff_4_clock_out),
    .Clock_Out(level_triggered_d_type_ff_5_clock_out), .Q(Q[4]));  // open: Q_Bar
  Level_Triggered_D_Type_Flip_Flop level_triggered_d_type_ff_6 (
    .Data(Data[5]), .Clock(level_triggered_d_type_ff_5_clock_out),
    .Clock_Out(level_triggered_d_type_ff_6_clock_out), .Q(Q[5]));  // open: Q_Bar
  Level_Triggered_D_Type_Flip_Flop level_triggered_d_type_ff_7 (
    .Data(Data[6]), .Clock(level_triggered_d_type_ff_6_clock_out),
    .Clock_Out(level_triggered_d_type_ff_7_clock_out), .Q(Q[6]));  // open: Q_Bar
  Level_Triggered_D_Type_Flip_Flop level_triggered_d_type_ff_8 (
    .Data(Data[7]), .Clock(level_triggered_d_type_ff_7_clock_out), .Q(Q[7]));  // open: Clock_Out, Q_Bar
endmodule

module _2_Line_To_1_Line_Selector (
  input  Select,
  input  B,
  input  A,
  output Out,
  output Select_Out
);

  wire and_1_out, and_2_out;

  not not_1 (Select_Out, Select);
  and and_1 (and_1_out, B, Select);
  and and_2 (and_2_out, A, Select_Out);
  or or_1 (Out, and_1_out, and_2_out);
endmodule

module _8_Bit_2_Line_To_1_Line_Selector (
  input  Select,
  input  [7:0] B,
  input  [7:0] A,
  output [7:0] Out
);

  wire n2_line_to_1_line_selector_1_select_out, n2_line_to_1_line_selector_2_select_out,
       n2_line_to_1_line_selector_3_select_out, n2_line_to_1_line_selector_4_select_out,
       n2_line_to_1_line_selector_5_select_out, n2_line_to_1_line_selector_6_select_out,
       n2_line_to_1_line_selector_7_select_out;

  _2_Line_To_1_Line_Selector u_2_line_to_1_line_selector_1 (
    .B(B[0]), .A(A[0]), .Select(Select), .Select_Out(n2_line_to_1_line_selector_1_select_out), .Out(Out[0]));
  _2_Line_To_1_Line_Selector u_2_line_to_1_line_selector_2 (
    .B(B[1]), .A(A[1]), .Select(n2_line_to_1_line_selector_1_select_out),
    .Select_Out(n2_line_to_1_line_selector_2_select_out), .Out(Out[1]));
  _2_Line_To_1_Line_Selector u_2_line_to_1_line_selector_3 (
    .B(B[2]), .A(A[2]), .Select(n2_line_to_1_line_selector_2_select_out),
    .Select_Out(n2_line_to_1_line_selector_3_select_out), .Out(Out[2]));
  _2_Line_To_1_Line_Selector u_2_line_to_1_line_selector_4 (
    .B(B[3]), .A(A[3]), .Select(n2_line_to_1_line_selector_3_select_out),
    .Select_Out(n2_line_to_1_line_selector_4_select_out), .Out(Out[3]));
  _2_Line_To_1_Line_Selector u_2_line_to_1_line_selector_5 (
    .B(B[4]), .A(A[4]), .Select(n2_line_to_1_line_selector_4_select_out),
    .Select_Out(n2_line_to_1_line_selector_5_select_out), .Out(Out[4]));
  _2_Line_To_1_Line_Selector u_2_line_to_1_line_selector_6 (
    .B(B[5]), .A(A[5]), .Select(n2_line_to_1_line_selector_5_select_out),
    .Select_Out(n2_line_to_1_line_selector_6_select_out), .Out(Out[5]));
  _2_Line_To_1_Line_Selector u_2_line_to_1_line_selector_7 (
    .B(B[6]), .A(A[6]), .Select(n2_line_to_1_line_selector_6_select_out),
    .Select_Out(n2_line_to_1_line_selector_7_select_out), .Out(Out[6]));
  _2_Line_To_1_Line_Selector u_2_line_to_1_line_selector_8 (
    .B(B[7]), .A(A[7]), .Select(n2_line_to_1_line_selector_7_select_out), .Out(Out[7]));  // open: Select_Out
endmodule

module circuit (
  input  [7:0] in_1
);

  wire [7:0] n8_bit_2_line_to_1_line_selector_1_out, n8_bit_latch_1_q, undriven;

  _8_Bit_Latch u_8_bit_latch_1 (.Data(undriven), .Q(n8_bit_latch_1_q));  // open: Clock
  _8_Bit_2_Line_To_1_Line_Selector u_8_bit_2_line_to_1_line_selector_1 (
    .B(n8_bit_latch_1_q), .A(in_1), .Out(n8_bit_2_line_to_1_line_selector_1_out));  // open: Select
  _8_Bit_Adder_Subtractor u_8_bit_adder_subtractor_1 (
    .Subtrahand8_0to7(n8_bit_2_line_to_1_line_selector_1_out), .Sub(1'b0));  // open: Minuend8_0to7, Overflow_Underflow, SumOut8_0to7
endmodule
